# Fritzing sketch hardwareaufbau (saved by Fritzing 0.9.10b)
breadboards: 1

parts:
  Part1 = Adafruit T-Cobbler Plus [part_number="Adafruit #1989 and #2028"]
  Mod1 = KY-012 Active Buzzer Module [package="Breakout board"]  # not connected
  JP1 = Header 6 [package=1x06-smd-female-v2]

nets:
  N1: Part1.+3.3V, JP1.1, JP1.2, JP1.5
  N2: Part1.SDA, JP1.3
  N3: Part1.SCL, JP1.4
  N4: Part1.GND, JP1.6

notes:
  GND VCC SCL SDA CSB SDO

custom parts:
  Adafruit T-Cobbler Plus: The Raspberry Pi has landed on the Maker World like a 40-GPIO pinned, quad-USB ported, credit card sized bomb of DIY joy. And while you can use most of our great Model B accessories by hooking up our downgrade cable, its probably a good time to upgrade your set up and accessorize using all of the 40 pins. That's why we now carry the Assembled Adafruit Pi T-Cobbler Plus - Breakout + Cable for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
  KY-012 Active Buzzer Module: Active Piezoelectric Buzzer Module KY-012, it produces single-tone sound when signal is high. (Special thanks to vanepp for fixing the PCB holes and other errors)
